# Fritzing sketch CablageAutofocus (saved by Fritzing 0.9.3b)
breadboards: 1

parts:
  Composant1 = Arduino Leonardo (Rev3b)
  WeMos_D1_Mini1 = WeMos D1 Mini
  LED2 = smd LED [color="Red (635nm)" package="1206 [SMD]"]
  LED1 = smd LED [color="Red (633nm)" package="0603 [SMD]"]

nets:
  N1: Composant1.D0/RX, WeMos_D1_Mini1.D8
  N2: Composant1.D1/TX, WeMos_D1_Mini1.D6
  N3: Composant1.D2/SDA, WeMos_D1_Mini1.D2
  N4: Composant1.D3_PWM/SCL, WeMos_D1_Mini1.D5
  N5: Composant1.D5_PWM, WeMos_D1_Mini1.D1
  N6: Composant1.D7, LED1.cathode
  5V: Composant1.5V, WeMos_D1_Mini1.5V
  N7: Composant1.GND, WeMos_D1_Mini1.G, LED2.anode, LED1.anode
  N8: Composant1.D8/A8, LED2.cathode
  N9: Composant1.D11_PWM, WeMos_D1_Mini1.D7
